# Fritzing sketch wiring_diagram (saved by Fritzing 0.9.2b)
breadboards: 1

parts:
  J1 = Piezo Speaker
  Part3 = Arduino Uno (Rev3) - ICSP
  Part4 = Matrix LED de 8x8 basada en MAX7219
  JP1 = Header 3 [package=screwterminal-3.5mm-3_lock.007s]

nets:
  GND: J1.pin1, Part3.GND, Part4.GND, JP1.2
  N1: J1.pin2, Part3.D0/RX
  N2: Part3.A0, JP1.3
  N3: Part3.D2, Part4.DIN
  N4: Part3.D3_PWM, Part4.CS
  N5: Part3.D4, Part4.CLK
  5V: Part3.5V, Part4.VCC, JP1.1
